# Fritzing sketch VOLBOX-breakout-arduino_v1 (saved by Fritzing 0.9.3b)
perfboards: 1

parts:
  Pro_Micro3 = Pro Micro
  ENCODER3 = Rotary Encoder with Knob
  ENCODER4 = Rotary Encoder with Knob
  ENCODER5 = Rotary Encoder with Knob
  LED3 = smd LED [color="Red (633nm)" package="0805 [SMD]"]
  LED4 = smd LED [color="Red (633nm)" package="0805 [SMD]"]
  LED5 = smd LED [color="Red (633nm)" package="0805 [SMD]"]
  SOURCE1 = Round Pushbutton
  DISABLE1 = Round Pushbutton
  RESET1 = Round Pushbutton
  R15 = Resistor [tolerance=±5% resistance=10k package="2010 [SMD]"]
  R16 = Resistor [tolerance=±5% resistance=10k package="2010 [SMD]"]
  R17 = Resistor [tolerance=±5% resistance=10k package="2010 [SMD]"]
  R18 = Resistor [tolerance=±5% resistance=10k package="2010 [SMD]"]
  R19 = Resistor [tolerance=±5% resistance=10k package="2010 [SMD]"]
  R20 = Resistor [tolerance=±5% resistance=10k package="2010 [SMD]"]
  R21 = Resistor [tolerance=±5% resistance=10k package="2010 [SMD]"]
  R22 = Resistor [tolerance=±5% resistance=10k package="2010 [SMD]"]
  R23 = Resistor [tolerance=±5% resistance=10k package="2010 [SMD]"]
  R24 = Resistor [tolerance=±5% resistance=10k package="2010 [SMD]"]
  R25 = Resistor [tolerance=±5% resistance=10k package="2010 [SMD]"]
  R26 = Resistor [tolerance=±5% resistance=220 package="2010 [SMD]"]
  R27 = Resistor [tolerance=±5% resistance=220 package="2010 [SMD]"]
  R28 = Resistor [tolerance=±5% resistance=220 package="2010 [SMD]"]

nets:
  N1: Pro_Micro3.GND, LED3.anode
  N2: Pro_Micro3.D16/MOSI, R28.Pin_0
  N3: Pro_Micro3.D14/MISO, R26.Pin_0
  N4: Pro_Micro3.D15/SCLK, R27.Pin_0
  N5: Pro_Micro3.VCC, ENCODER3.no_name_yet#4
  N6: Pro_Micro3.RST, RESET1.leg1
  N7: ENCODER3.no_name_yet#1, R23.Pin_1
  N8: ENCODER3.no_name_yet#3, R24.Pin_1
  N9: ENCODER3.no_name_yet#5, R17.Pin_0
  N10: ENCODER4.no_name_yet#1, R21.Pin_1
  N11: ENCODER4.no_name_yet#3, R22.Pin_1
  N12: ENCODER4.no_name_yet#5, R16.Pin_0
  N13: ENCODER5.no_name_yet#1, R19.Pin_1
  N14: ENCODER5.no_name_yet#3, R20.Pin_1
  N15: ENCODER5.no_name_yet#5, R15.Pin_0
  N16: LED3.cathode, R28.Pin_1
  N17: LED4.cathode, R27.Pin_1
  N18: LED5.cathode, R26.Pin_1
  N19: SOURCE1.leg1, R18.Pin_0
  N20: DISABLE1.leg1, R25.Pin_1

notes:
  DISABLE
  + LED2
  + LED0
  ENCODER0
  + LED1
  ENCODER2
  RESET
  SOURCE
  ENCODER1

custom parts:
  Pro Micro: The SparkFun Pro Micro is a complete USB-based microcontoller development system, in a very small footprint, capable of implementing many types of projects. All programming can be done via the USB port.
  Rotary Encoder with Knob: Rotary Encoder with 1/4" Shaft and Knob
