# Fritzing sketch VOLBOX-breakout-final_v1 (saved by Fritzing 0.9.3b)
perfboards: 3

parts:
  Pro_Micro2 = Pro Micro
  ENCODER0 = Rotary Encoder with Knob
  ENCODER1 = Rotary Encoder with Knob
  ENCODER2 = Rotary Encoder with Knob
  LED0 = smd LED [color="Red (633nm)" package="0805 [SMD]"]
  LED1 = smd LED [color="Red (633nm)" package="0805 [SMD]"]
  LED2 = smd LED [color="Red (633nm)" package="0805 [SMD]"]
  DISABLE = Round Pushbutton
  SOURCE = Round Pushbutton
  RESET = Round Pushbutton
  R1 = Resistor [tolerance=±5% resistance=10k package="2010 [SMD]"]
  R2 = Resistor [tolerance=±5% resistance=10k package="2010 [SMD]"]
  R3 = Resistor [tolerance=±5% resistance=10k package="2010 [SMD]"]
  R4 = Resistor [tolerance=±5% resistance=10k package="2010 [SMD]"]
  R5 = Resistor [tolerance=±5% resistance=10k package="2010 [SMD]"]
  R6 = Resistor [tolerance=±5% resistance=10k package="2010 [SMD]"]
  R7 = Resistor [tolerance=±5% resistance=10k package="2010 [SMD]"]
  R8 = Resistor [tolerance=±5% resistance=10k package="2010 [SMD]"]
  R9 = Resistor [tolerance=±5% resistance=10k package="2010 [SMD]"]
  R10 = Resistor [tolerance=±5% resistance=10k package="2010 [SMD]"]
  R11 = Resistor [tolerance=±5% resistance=10k package="2010 [SMD]"]
  R12 = Resistor [tolerance=±5% resistance=220 package="2010 [SMD]"]
  R13 = Resistor [tolerance=±5% resistance=220 package="2010 [SMD]"]
  R14 = Resistor [tolerance=±5% resistance=220 package="2010 [SMD]"]
  SPKR1 = Loudspeaker  # not connected
  SUB_CONTROL_POT = Rotary Potentiometer (Large) [maximum_resistance=10kΩ package=THT]  # not connected
  STEREO_POT_RIGHT = Rotary Potentiometer (Large) [maximum_resistance=100kΩ package=THT]
  STERO_POT_LEFT = Rotary Potentiometer (Large) [maximum_resistance=100kΩ package=THT]
  LOGITECH_POWER_LED = smd LED [color="Orange (620nm)" package="0805 [SMD]"]  # not connected
  AUDIO_INPUT = 2.5mm Audio Jack [package=stereojack2.5mm_smd]  # not connected
  AUDIO_OUTPUT = 2.5mm Audio Jack [package=stereojack2.5mm_smd]  # not connected
  LOGITECH_POWER_BUTTON = SWITCH-DPDT [package=ayz0202]  # not connected
  U1 = Transformer [package=transformer]  # not connected
  Power_plug1 = Power plug  # not connected

nets:
  N1: Pro_Micro2.GND, LED2.anode
  N2: Pro_Micro2.D16/MOSI, R12.Pin_0
  N3: Pro_Micro2.D14/MISO, R14.Pin_0
  N4: Pro_Micro2.D15/SCLK, R13.Pin_0
  N5: Pro_Micro2.VCC, ENCODER2.no_name_yet#4
  N6: Pro_Micro2.RST, RESET.leg1
  N7: ENCODER0.no_name_yet#1, R7.Pin_1
  N8: ENCODER0.no_name_yet#3, R6.Pin_1
  N9: ENCODER0.no_name_yet#5, R11.Pin_0
  N10: ENCODER1.no_name_yet#1, R5.Pin_1
  N11: ENCODER1.no_name_yet#3, R4.Pin_1
  N12: ENCODER1.no_name_yet#5, R10.Pin_0
  N13: ENCODER2.no_name_yet#1, R3.Pin_1
  N14: ENCODER2.no_name_yet#3, R2.Pin_1
  N15: ENCODER2.no_name_yet#5, R9.Pin_0
  N16: LED0.cathode, R14.Pin_1
  N17: LED1.cathode, R13.Pin_1
  N18: LED2.cathode, R12.Pin_1
  N19: DISABLE.leg1, R1.Pin_1
  N20: SOURCE.leg1, R8.Pin_0
  N21: STEREO_POT_RIGHT.leg2, STERO_POT_LEFT.leg2

notes:
  SUB SPEAKER
  DUALGANG/STEREO POT.
  LOGITECH MAIN VOL. CONTROL
  10KΩ LOGARITHMIC
  STANDARD POT.
  LOGITECH SUB VOL. CONTROL
  LOGITECH POWER LED
  ORANGE LED
  AUDIO INPUT
  2.5MM AUDIO JACK
  LOGITECH WIRED CONTROLLER PCB
  LOGITECH AUDIO AMP. PCB
  SUB TRANSFORMER
  POWER SWITCH
  DPDT LATCHING
  POWER PLUG
  2-PRONG
  DISABLE
  SOURCE
  RESET
  ENCODER0
  + LED0
  + LED1
  ENCODER1
  + LED2
  ENCODER2

custom parts:
  Pro Micro: The SparkFun Pro Micro is a complete USB-based microcontoller development system, in a very small footprint, capable of implementing many types of projects. All programming can be done via the USB port.
  Rotary Encoder with Knob: Rotary Encoder with 1/4" Shaft and Knob
