# Fritzing sketch VOLBOX-breakout-logitech_v1 (saved by Fritzing 0.9.3b)
perfboards: 2

parts:
  STEREO_POT_RIGHT1 = Rotary Potentiometer (Large) [maximum_resistance=100kΩ package=THT]
  LOGITECH_POWER_LED1 = smd LED [color="Orange (620nm)" package="0805 [SMD]"]  # not connected
  SPKR2 = Loudspeaker  # not connected
  STERO_POT_LEFT1 = Rotary Potentiometer (Large) [maximum_resistance=100kΩ package=THT]
  SUB_CONTROL_POT_1 = Rotary Potentiometer (Large) [maximum_resistance=10kΩ package=THT]  # not connected
  AUDIO_OUTPUT1 = 2.5mm Audio Jack [package=stereojack2.5mm_smd]  # not connected
  AUDIO_INPUT1 = 2.5mm Audio Jack [package=stereojack2.5mm_smd]  # not connected
  LOGITECH_POWER_BUTTON1 = SWITCH-DPDT [package=ayz0202]  # not connected
  U2 = Transformer [package=transformer]  # not connected
  Power_plug2 = Power plug  # not connected

nets:
  N1: STEREO_POT_RIGHT1.leg2, STERO_POT_LEFT1.leg2

notes:
  10KΩ LOGARITHMIC
  LOGITECH SUB VOL. CONTROL
  STANDARD POT.
  LOGITECH MAIN VOL. CONTROL
  POWER SWITCH
  POWER PLUG
  LOGITECH AUDIO AMP. PCB
  LOGITECH WIRED CONTROLLER PCB
  AUDIO INPUT
  LOGITECH POWER LED
  DUALGANG/STEREO POT.
  2-PRONG
  DPDT LATCHING
  2.5MM AUDIO JACK
  ORANGE LED
  SUB SPEAKER
  SUB TRANSFORMER
