# Fritzing sketch volbox-bb-3re-v4 (saved by Fritzing 0.9.3b)
breadboards: 1

parts:
  Pro_Micro1 = Pro Micro
  R1 = Resistor [tolerance=±5% resistance=10k package="2010 [SMD]"]
  R2 = Resistor [tolerance=±5% resistance=10k package="2010 [SMD]"]
  R3 = Resistor [tolerance=±5% resistance=10k package="2010 [SMD]"]
  R4 = Resistor [tolerance=±5% resistance=10k package="2010 [SMD]"]
  R5 = Resistor [tolerance=±5% resistance=10k package="2010 [SMD]"]
  R6 = Resistor [tolerance=±5% resistance=10k package="2010 [SMD]"]
  ENCODER0 = Rotary Encoder with Knob
  ENCODER1 = Rotary Encoder with Knob
  R7 = Resistor [tolerance=±5% resistance=10k package="2010 [SMD]"]
  R8 = Resistor [tolerance=±5% resistance=10k package="2010 [SMD]"]
  R9 = Resistor [tolerance=±5% resistance=10k package="2010 [SMD]"]
  R10 = Resistor [tolerance=±5% resistance=10k package="2010 [SMD]"]
  ENCODER2 = Rotary Encoder with Knob
  LED2 = smd LED [color="Red (633nm)" package="0805 [SMD]"]
  LED3 = smd LED [color="Red (633nm)" package="0805 [SMD]"]
  LED4 = smd LED [color="Red (633nm)" package="0805 [SMD]"]
  R12 = Resistor [tolerance=±5% resistance=220 package="2010 [SMD]"]
  R13 = Resistor [tolerance=±5% resistance=220 package="2010 [SMD]"]
  R14 = Resistor [tolerance=±5% resistance=220 package="2010 [SMD]"]
  SOURCE = Round Pushbutton
  R15 = Resistor [tolerance=±5% resistance=10k package="2010 [SMD]"]
  SUSPEND = Round Pushbutton
  RESET = Round Pushbutton

nets:
  N1: Pro_Micro1.TX1, ENCODER2.no_name_yet#1
  N2: Pro_Micro1.RX0, ENCODER2.no_name_yet#3
  N3: Pro_Micro1.GND, R3.Pin_1, R6.Pin_1, ENCODER0.no_name_yet#2, ENCODER1.no_name_yet#2, R9.Pin_1, R10.Pin_1, ENCODER2.no_name_yet#2, LED2.anode, LED3.anode, R15.Pin_1, RESET.leg0
  N4: Pro_Micro1.D2, ENCODER0.no_name_yet#1
  N5: Pro_Micro1.D3, ENCODER0.no_name_yet#3
  N6: Pro_Micro1.D4, ENCODER0.no_name_yet#5
  N7: Pro_Micro1.D5, ENCODER1.no_name_yet#5
  N8: Pro_Micro1.D6, ENCODER1.no_name_yet#3
  N9: Pro_Micro1.D7, ENCODER1.no_name_yet#1
  N10: Pro_Micro1.D8, ENCODER2.no_name_yet#5
  N11: Pro_Micro1.D9, R15.Pin_0, SUSPEND.leg1
  N12: Pro_Micro1.D10, R14.Pin_1
  N13: Pro_Micro1.D16/MOSI, R10.Pin_0, SOURCE.leg1
  N14: Pro_Micro1.D14/MISO, R12.Pin_1
  N15: Pro_Micro1.D15/SCLK, R13.Pin_1
  N16: Pro_Micro1.VCC, R1.Pin_0, R2.Pin_0, R4.Pin_0, R5.Pin_0, ENCODER0.no_name_yet#4, ENCODER1.no_name_yet#4, R7.Pin_0, R8.Pin_0, ENCODER2.no_name_yet#4, SOURCE.leg0, SUSPEND.leg0
  N17: Pro_Micro1.RST, RESET.leg1
  N18: LED2.cathode, R12.Pin_0
  N19: LED3.cathode, R13.Pin_0
  N20: LED4.cathode, R14.Pin_0

custom parts:
  Pro Micro: The SparkFun Pro Micro is a complete USB-based microcontoller development system, in a very small footprint, capable of implementing many types of projects. All programming can be done via the USB port.
  Rotary Encoder with Knob: Rotary Encoder with 1/4" Shaft and Knob
