# Fritzing sketch volbox-bo-3re-v1 (saved by Fritzing 0.9.3b)
perfboards: 1

parts:
  R1_(RE0) = Resistor [tolerance=±5% resistance=10k package="0805 [SMD]"]  # not connected
  R2_(RE0) = Resistor [tolerance=±5% resistance=10k package="0805 [SMD]"]  # not connected
  R3_(RE0) = Resistor [tolerance=±5% resistance=10k package="0805 [SMD]"]  # not connected
  R4_(RE2) = Resistor [tolerance=±5% resistance=10k package="0805 [SMD]"]  # not connected
  R5_(SW0) = Resistor [tolerance=±5% resistance=10k package="0805 [SMD]"]  # not connected
  R6_(RE1) = Resistor [tolerance=±5% resistance=10k package="0805 [SMD]"]  # not connected
  R7_(RE1) = Resistor [tolerance=±5% resistance=10k package="0805 [SMD]"]  # not connected
  R8_(RE1) = Resistor [tolerance=±5% resistance=10k package="0805 [SMD]"]  # not connected
  R9_(RE2) = Resistor [tolerance=±5% resistance=10k package="0805 [SMD]"]  # not connected
  R11_(LED0) = Resistor [tolerance=±5% resistance=220 package="0805 [SMD]"]
  R10_(RE2) = Resistor [tolerance=±5% resistance=10k package="0805 [SMD]"]  # not connected
  R12_(LED1) = Resistor [tolerance=±5% resistance=220 package="0805 [SMD]"]
  R13_(LED2) = Resistor [tolerance=±5% resistance=220 package="0805 [SMD]"]
  R14_(SW1) = Resistor [tolerance=±5% resistance=10k package="0805 [SMD]"]  # not connected
  PRO_MICRO = Pro Micro
  ENCODER0 = Rotary Encoder with Knob
  ENCODER1 = Rotary Encoder with Knob
  ENCODER2 = Rotary Encoder with Knob
  LED0 = smd LED [color="Red (633nm)" package="0805 [SMD]"]
  LED1 = smd LED [color="Red (633nm)" package="0805 [SMD]"]
  LED2 = smd LED [color="Red (633nm)" package="0805 [SMD]"]
  SOURCE = Round Pushbutton
  SUSPEND = Round Pushbutton
  RESET = Round Pushbutton

nets:
  N1: R11_(LED0).Pin_0, PRO_MICRO.D14/MISO
  N2: R11_(LED0).Pin_1, LED0.cathode
  N3: R12_(LED1).Pin_0, PRO_MICRO.D15/SCLK
  N4: R12_(LED1).Pin_1, LED1.cathode
  N5: R13_(LED2).Pin_0, PRO_MICRO.D10
  N6: R13_(LED2).Pin_1, LED2.cathode
  N7: PRO_MICRO.TX1, ENCODER2.no_name_yet#1
  N8: PRO_MICRO.RX0, ENCODER2.no_name_yet#3
  N9: PRO_MICRO.D2, ENCODER0.no_name_yet#1
  N10: PRO_MICRO.D3, ENCODER0.no_name_yet#3
  N11: PRO_MICRO.D4, ENCODER0.no_name_yet#5
  N12: PRO_MICRO.D5, ENCODER1.no_name_yet#5
  N13: PRO_MICRO.D6, ENCODER1.no_name_yet#3
  N14: PRO_MICRO.D7, ENCODER1.no_name_yet#1
  N15: PRO_MICRO.D8, ENCODER2.no_name_yet#5
  N16: PRO_MICRO.D9, SUSPEND.leg0
  N17: PRO_MICRO.D16/MOSI, SOURCE.leg0
  N18: PRO_MICRO.VCC, ENCODER0.no_name_yet#4, ENCODER1.no_name_yet#4, ENCODER2.no_name_yet#4
  N19: PRO_MICRO.RST, RESET.leg0
  N20: PRO_MICRO.GND, ENCODER0.no_name_yet#2, ENCODER1.no_name_yet#2, LED0.anode, LED1.anode, LED2.anode, RESET.leg1

custom parts:
  Pro Micro: The SparkFun Pro Micro is a complete USB-based microcontoller development system, in a very small footprint, capable of implementing many types of projects. All programming can be done via the USB port.
  Rotary Encoder with Knob: Rotary Encoder with 1/4" Shaft and Knob
